// Logisim project mux_2.circ as structural Verilog: 1 circuit, main circuit main
module main (
  input  in_1,
  input  in_2,
  input  in_3,
  input  in_4,
  input  in_5,
  input  in_6,
  input  in_7,
  input  in_8,
  input  in_9,
  input  in_10,
  input  in_11,
  input  in_12,
  input  in_13,
  input  in_14,
  input  in_15
);

  wire multiplexer_1_out, multiplexer_2_out, multiplexer_3_out, multiplexer_4_out, multiplexer_5_out,
       multiplexer_6_out, multiplexer_7_out;

  Multiplexer multiplexer_1 (.in0(in_1), .in1(in_2), .out(multiplexer_1_out), .sel(in_3));
  Multiplexer multiplexer_2 (.in0(in_4), .in1(in_6), .out(multiplexer_2_out), .sel(in_7));
  Multiplexer multiplexer_3 (.in0(in_8), .in1(in_10), .out(multiplexer_3_out), .sel(in_11));
  Multiplexer multiplexer_4 (.in0(in_12), .in1(in_14), .out(multiplexer_4_out), .sel(in_15));
  Multiplexer multiplexer_5 (.in0(multiplexer_1_out), .in1(multiplexer_2_out), .out(multiplexer_5_out), .sel(in_5));
  Multiplexer multiplexer_6 (.in0(multiplexer_3_out), .in1(multiplexer_4_out), .out(multiplexer_6_out), .sel(in_13));
  Multiplexer multiplexer_7 (.in0(multiplexer_5_out), .in1(multiplexer_6_out), .out(multiplexer_7_out), .sel(in_9));
  LED led_1 (.in(multiplexer_7_out));
endmodule
